# Fritzing sketch WeMosD1Mini (saved by Fritzing 0.9.3b)
breadboards: 1

parts:
  WeMos_D1_Mini1 = WeMos D1 Mini
  LED1 = LED - 5mm [color="Red (633nm)" package="5 mm [THT]"]
  LED2 = LED - 5mm [color="Red (633nm)" package="5 mm [THT]"]
  LED3 = LED - 5mm [color="Red (633nm)" package="5 mm [THT]"]
  LED4 = LED - 5mm [color="Red (633nm)" package="5 mm [THT]"]
  LED5 = LED - 5mm [color="Red (633nm)" package="5 mm [THT]"]
  LED6 = LED - 5mm [color="Red (633nm)" package="5 mm [THT]"]
  LED7 = LED - 5mm [color="Red (633nm)" package="5 mm [THT]"]
  LED8 = LED - 5mm [color="Red (633nm)" package="5 mm [THT]"]
  LED9 = LED - 5mm [color="Red (633nm)" package="5 mm [THT]"]
  LED10 = LED - 5mm [color="Red (633nm)" package="5 mm [THT]"]
  LED11 = LED - 5mm [color="Red (633nm)" package="5 mm [THT]"]

nets:
  N1: WeMos_D1_Mini1.D0, LED11.anode
  N2: WeMos_D1_Mini1.D1, LED3.anode
  N3: WeMos_D1_Mini1.D2, LED4.anode
  N4: WeMos_D1_Mini1.D3, LED5.anode
  N5: WeMos_D1_Mini1.D4, LED6.anode
  N6: WeMos_D1_Mini1.D5, LED10.anode
  N7: WeMos_D1_Mini1.D6, LED9.anode
  N8: WeMos_D1_Mini1.D7, LED8.anode
  N9: WeMos_D1_Mini1.D8, LED7.anode
  N10: WeMos_D1_Mini1.G, LED1.cathode, LED2.cathode, LED3.cathode, LED4.cathode, LED5.cathode, LED6.cathode, LED7.cathode, LED8.cathode, LED9.cathode, LED10.cathode, LED11.cathode
  N11: WeMos_D1_Mini1.RX, LED2.anode
  N12: WeMos_D1_Mini1.TX, LED1.anode
