# Fritzing sketch WeMosD1R2 (saved by Fritzing 0.9.3b)
breadboards: 1

parts:
  LED12 = LED - 5mm [color="Red (633nm)" package="5 mm [THT]"]
  LED13 = LED - 5mm [color="Red (633nm)" package="5 mm [THT]"]
  LED14 = LED - 5mm [color="Red (633nm)" package="5 mm [THT]"]
  LED15 = LED - 5mm [color="Red (633nm)" package="5 mm [THT]"]
  LED16 = LED - 5mm [color="Red (633nm)" package="5 mm [THT]"]
  LED17 = LED - 5mm [color="Red (633nm)" package="5 mm [THT]"]
  LED18 = LED - 5mm [color="Red (633nm)" package="5 mm [THT]"]
  LED19 = LED - 5mm [color="Red (633nm)" package="5 mm [THT]"]
  LED20 = LED - 5mm [color="Red (633nm)" package="5 mm [THT]"]
  LED21 = LED - 5mm [color="Red (633nm)" package="5 mm [THT]"]
  LED22 = LED - 5mm [color="Red (633nm)" package="5 mm [THT]"]
  WeMos_D1_R1 = WeMos D1 R2

nets:
  N1: LED12.cathode, LED13.cathode, LED14.cathode, LED15.cathode, LED16.cathode, LED17.cathode, LED18.cathode, LED19.cathode, LED20.cathode, LED21.cathode, LED22.cathode, WeMos_D1_R1.GND
  N2: LED12.anode, WeMos_D1_R1.TX
  N3: LED13.anode, WeMos_D1_R1.RX
  N4: LED14.anode, WeMos_D1_R1.SCL/D1
  N5: LED15.anode, WeMos_D1_R1.SDA/D2
  N6: LED16.anode, WeMos_D1_R1.D3
  N7: LED17.anode, WeMos_D1_R1.D4
  N8: LED18.anode, WeMos_D1_R1.SS/D8
  N9: LED19.anode, WeMos_D1_R1.D7
  N10: LED20.anode, WeMos_D1_R1.D6
  N11: LED21.anode, WeMos_D1_R1.D5
  N12: LED22.anode, WeMos_D1_R1.D0

custom parts:
  WeMos D1 R2: The WeMos D1 R2 is a wifi board based on the ESP8266
