# Fritzing sketch Mega (saved by Fritzing 0.9.3b)
breadboards: 2

parts:
  8x8_LED_matrix_MAX1 = 8x8 Red 8x8 LED Matrix with MAX7219
  8x8_LED_matrix_MAX2 = 8x8 Red 8x8 LED Matrix with MAX7219
  8x8_LED_matrix_MAX3 = 8x8 Red 8x8 LED Matrix with MAX7219
  8x8_LED_matrix_MAX4 = 8x8 Red 8x8 LED Matrix with MAX7219
  microSD_Transflash3 = SparkFun - microSD Transflash
  Componente2 = Arduino Mega ADK (Rev3)

nets:
  VCC: 8x8_LED_matrix_MAX1.VCC, 8x8_LED_matrix_MAX1.VCC_PT, 8x8_LED_matrix_MAX2.VCC, 8x8_LED_matrix_MAX2.VCC_PT, 8x8_LED_matrix_MAX3.VCC, 8x8_LED_matrix_MAX3.VCC_PT, 8x8_LED_matrix_MAX4.VCC, 8x8_LED_matrix_MAX4.VCC_PT, Componente2.5V
  GND: 8x8_LED_matrix_MAX1.GND, 8x8_LED_matrix_MAX1.CLK_PT, 8x8_LED_matrix_MAX2.GND, 8x8_LED_matrix_MAX2.CLK_PT, 8x8_LED_matrix_MAX3.GND, 8x8_LED_matrix_MAX3.CLK_PT, 8x8_LED_matrix_MAX4.GND, 8x8_LED_matrix_MAX4.CLK_PT, microSD_Transflash3.GND, Componente2.GND
  N1: 8x8_LED_matrix_MAX1.GND_PT, 8x8_LED_matrix_MAX1.CLK, 8x8_LED_matrix_MAX2.GND_PT, 8x8_LED_matrix_MAX2.CLK, 8x8_LED_matrix_MAX3.GND_PT, 8x8_LED_matrix_MAX3.CLK, 8x8_LED_matrix_MAX4.GND_PT, 8x8_LED_matrix_MAX4.CLK, Componente2.D2_PWM
  N2: 8x8_LED_matrix_MAX1.DIN, Componente2.D4_PWM
  N3: 8x8_LED_matrix_MAX1.DIN_CHN, 8x8_LED_matrix_MAX1.CS, 8x8_LED_matrix_MAX2.DIN, 8x8_LED_matrix_MAX2.DIN_CHN, 8x8_LED_matrix_MAX2.CS, 8x8_LED_matrix_MAX3.DIN, 8x8_LED_matrix_MAX3.DIN_CHN, 8x8_LED_matrix_MAX3.CS, 8x8_LED_matrix_MAX4.DIN, 8x8_LED_matrix_MAX4.DIN_CHN, 8x8_LED_matrix_MAX4.CS, Componente2.D3_PWM
  N4: microSD_Transflash3.DO, Componente2.D50/MISO
  N5: microSD_Transflash3.SCK, Componente2.D52/SCK
  VCC_2: microSD_Transflash3.VCC, Componente2.3V3
  N6: microSD_Transflash3.DI, Componente2.D51/MOSI
  N7: microSD_Transflash3.CS, Componente2.D53/SS

custom parts:
  8x8 Red 8x8 LED Matrix with MAX7219: Description: 8 by 8 red LED matrix with a MAX7219 controller.

// code stored in the sketch: a006resistencias.ino
/*
  Autor: Ramón Junquera
  
  Tema: Lectura y escritura de señales digitales
  
  Objetivo: Funcionamiento de las resistencias de seguridad y de la breadboard
  
  Material adicional: breadboard, led, resistencia, cables

  Descripción:
  El ejemplo es el mismo que el utilizado en el ejemplo de blink. Se hace parpadear un led conectado al pin 13.
  La diferencia es que utilizaremos una breadboard para montar un led externo y le pondremos una resistencia de seguridad.
  LED significa Light Emiting Diode. Son diodos que se iluminan cuando pasa la electricidad.
  Un led tiene polaridad. Si se conecta con la polaridad invertida puede quemarse.
  Sus conexiones se diferencian para poder conectar siempre correctamente.
  La pata más larga es el ánodo, o pata positiva. Siempre se conecta a la fuente de alimentación o pin.
  La pata más corta es el cátodo, o pata negativa. Siempre se conecta a tierra (GND).
  Un led siempre debe ir acompañado de una resistencia para proteger el microcontrolador de la placa.
  El rango intensidad adecuado para el correcto funcionamiento de un led es de 5 a 20mA.
  Para que un led se ilumine bien, sin llegar al límite, se considera que necesita 15mA (0.015A).
  Arduino trabaja con una diferencia de potencial (voltaje) de 5V.
  El led consume unos 2V, así que necesitamos una resistencia que consuma los otros 3.
  Puesto que V=I*R (Voltaje = Intensidad * Resistencia)
  Deducimos que R=V/I=3V/0.015A=200 ohmios.
  Si aumentamos la resistencia en un 10% (por seguridad) para asegurarnos que nunca llegaremos al límite máximo
  tenemos que necesitamos que un led siempre tenga asociada una resistencia de 220 ohmios.
  Distinguimos una resistencia de 220 ohmios porque tiene las siguientes bandas:
  - Banda 1 = roja = 2
  - Banda 2 = roja = 2
  - Banda 3 = negra = 0
  - Banda 4 = negra = multiplicador *1
  - Banda 5 = dorada = tolerancia +-5%
  Para que la resistencia haga su trabajo de reducción de voltaje debemos encadenar los elementos de la siguiente manera:
  - Pin o fuentee de alimentación (polo positivo)
  - Resistencia de 220 ohmios
  - Ánodo (pata larga) del led
  - Cátodo (pata corta) del led
  - Tierra (GND o polo negativo)
  Si queremos ser exactos, no todos los leds consumen el mismo voltaje. Depende del color. Esta es la tabla correcta:
    1.7V : rojo de bajo brillo
    1.9V : rojo de alto brillo, alta eficacia y baja corriente
    2.0V : naranja y amarillo
    2.1V : verde
    3.4V : blanco brilante, verde brillante y azul
    4.6V : azul brillante y leds especializados
  El led que está integrado en placa ya tiene tambien en placa su resistencia asociada.
  
  Resultado:
  El led externo parpadea al unísono con el que está integrado en placa.
*/

// the setup function runs once when you press reset or power the board
void setup() {
  //Configuramos el pin 13 como salida para poder escribir en él
  pinMode(13, OUTPUT);
}

// the loop function runs over and over again forever
void loop() {
  digitalWrite(13, HIGH);   //Encendemos el led
  delay(1000);              //Esperamos un segundo
  digitalWrite(13, LOW);    //Apagamos el led
  delay(1000);              //Esperamos otro segundo
}
