# Fritzing sketch UNO (saved by Fritzing 0.9.3b)
breadboards: 1

parts:
  Parte1 = Arduino Uno (Rev3)
  R5 = Resistor [tolerance=±1% resistance=220 package=THT]
  R7 = Resistor [tolerance=±1% resistance=220 package=THT]
  U1 = 7-SEGMENT-4DIGIT [package=7-segment-4digit-5641]
  R8 = Resistor [tolerance=±1% resistance=220 package=THT]
  R9 = Resistor [tolerance=±1% resistance=220 package=THT]

nets:
  N1: Parte1.D8, U1.F
  N2: Parte1.D9_PWM, U1.E
  N3: Parte1.D10_PWM/SS, U1.D
  N4: Parte1.D11_PWM/MOSI, U1.C
  N5: Parte1.D12/MISO, U1.B
  N6: Parte1.D13/SCK, U1.A
  N7: Parte1.D2, R9.Pin_1
  N8: Parte1.D3_PWM, R5.Pin_1
  N9: Parte1.D4, R8.Pin_1
  N10: Parte1.D5_PWM, R7.Pin_0
  N11: Parte1.D7, U1.G
  N12: R5.Pin_0, U1.DIG3
  N13: R7.Pin_1, U1.DIG1
  N14: U1.DIG2, R8.Pin_0
  N15: U1.DIG4, R9.Pin_0

custom parts:
  7-SEGMENT-4DIGIT: if you need make parts, send me e-mail and write. Price 1 part=0.9 WMZ (http://www.wmtransfer.com/) ~ 0.9 Euro

// code stored in the sketch: a006resistencias.ino
/*
  Autor: Ramón Junquera
  
  Tema: Lectura y escritura de señales digitales
  
  Objetivo: Funcionamiento de las resistencias de seguridad y de la breadboard
  
  Material adicional: breadboard, led, resistencia, cables

  Descripción:
  El ejemplo es el mismo que el utilizado en el ejemplo de blink. Se hace parpadear un led conectado al pin 13.
  La diferencia es que utilizaremos una breadboard para montar un led externo y le pondremos una resistencia de seguridad.
  LED significa Light Emiting Diode. Son diodos que se iluminan cuando pasa la electricidad.
  Un led tiene polaridad. Si se conecta con la polaridad invertida puede quemarse.
  Sus conexiones se diferencian para poder conectar siempre correctamente.
  La pata más larga es el ánodo, o pata positiva. Siempre se conecta a la fuente de alimentación o pin.
  La pata más corta es el cátodo, o pata negativa. Siempre se conecta a tierra (GND).
  Un led siempre debe ir acompañado de una resistencia para proteger el microcontrolador de la placa.
  El rango intensidad adecuado para el correcto funcionamiento de un led es de 5 a 20mA.
  Para que un led se ilumine bien, sin llegar al límite, se considera que necesita 15mA (0.015A).
  Arduino trabaja con una diferencia de potencial (voltaje) de 5V.
  El led consume unos 2V, así que necesitamos una resistencia que consuma los otros 3.
  Puesto que V=I*R (Voltaje = Intensidad * Resistencia)
  Deducimos que R=V/I=3V/0.015A=200 ohmios.
  Si aumentamos la resistencia en un 10% (por seguridad) para asegurarnos que nunca llegaremos al límite máximo
  tenemos que necesitamos que un led siempre tenga asociada una resistencia de 220 ohmios.
  Distinguimos una resistencia de 220 ohmios porque tiene las siguientes bandas:
  - Banda 1 = roja = 2
  - Banda 2 = roja = 2
  - Banda 3 = negra = 0
  - Banda 4 = negra = multiplicador *1
  - Banda 5 = dorada = tolerancia +-5%
  Para que la resistencia haga su trabajo de reducción de voltaje debemos encadenar los elementos de la siguiente manera:
  - Pin o fuentee de alimentación (polo positivo)
  - Resistencia de 220 ohmios
  - Ánodo (pata larga) del led
  - Cátodo (pata corta) del led
  - Tierra (GND o polo negativo)
  Si queremos ser exactos, no todos los leds consumen el mismo voltaje. Depende del color. Esta es la tabla correcta:
    1.7V : rojo de bajo brillo
    1.9V : rojo de alto brillo, alta eficacia y baja corriente
    2.0V : naranja y amarillo
    2.1V : verde
    3.4V : blanco brilante, verde brillante y azul
    4.6V : azul brillante y leds especializados
  El led que está integrado en placa ya tiene tambien en placa su resistencia asociada.
  
  Resultado:
  El led externo parpadea al unísono con el que está integrado en placa.
*/

// the setup function runs once when you press reset or power the board
void setup() {
  //Configuramos el pin 13 como salida para poder escribir en él
  pinMode(13, OUTPUT);
}

// the loop function runs over and over again forever
void loop() {
  digitalWrite(13, HIGH);   //Encendemos el led
  delay(1000);              //Esperamos un segundo
  digitalWrite(13, LOW);    //Apagamos el led
  delay(1000);              //Esperamos otro segundo
}
