# Fritzing sketch WeMosLolin32 (saved by Fritzing 0.9.3b)
breadboards: 1

parts:
  U2 = lolin
  led_display2 = Catalex 4-digits led display

nets:
  N1: U2.connector11, led_display2.CLK
  N2: U2.connector13, led_display2.DIO
  N3: U2.connector25, led_display2.VCC
  N4: U2.connector30, led_display2.GND
