# Fritzing sketch RPi3 (saved by Fritzing 0.9.3b)
breadboards: 2

parts:
  C12 = Ceramic Capacitor [capacitance=10µF package="1206 [SMD, multilayer]"]
  C13 = Ceramic Capacitor [capacitance="100 nF" package="1206 [SMD, multilayer]"]
  U13 = MAX7219 [package=dil24]
  R5 = Resistor [tolerance=±1% resistance=10k package=THT]
  8x8_LED_Matrix1 = 8x8 LED Matrix 1388ASR
  Raspberry_Pi_3 = Raspberry Pi 3 [part_number=RPI-3-V1.2]

nets:
  3V3: C12.0, C13.1, U13.VCC, R5.Pin_1, Raspberry_Pi_3.3v3, Raspberry_Pi_3.3V3, Raspberry_Pi_3.5V
  GND: C12.1, C13.0, U13.GND, U13.GND2, Raspberry_Pi_3.GND
  N1: U13.DIN, Raspberry_Pi_3.GPIO21
  N2: U13.DIG0, 8x8_LED_Matrix1.Pin_9
  N3: U13.DIG4, 8x8_LED_Matrix1.Pin_1
  N4: U13.DIG2, 8x8_LED_Matrix1.Pin_8
  N5: U13.DIG3, 8x8_LED_Matrix1.Pin_12
  N6: U13.DIG7, 8x8_LED_Matrix1.Pin_5
  N7: U13.DIG5, 8x8_LED_Matrix1.Pin_7#7
  N8: U13.DIG1, 8x8_LED_Matrix1.Pin14
  N9: U13.LOAD, Raspberry_Pi_3.GPIO20
  N10: U13.CLK, Raspberry_Pi_3.GPIO16
  N11: U13.SEGA, 8x8_LED_Matrix1.Pin_3
  N12: U13.SEGF, 8x8_LED_Matrix1.Pin_15
  N13: U13.SEGB, 8x8_LED_Matrix1.Pin_4
  N14: U13.SEGG, 8x8_LED_Matrix1.Pin_16
  N15: U13.ISET, R5.Pin_0
  N16: U13.SEGC, 8x8_LED_Matrix1.Pin_7#10
  N17: U13.SEGE, 8x8_LED_Matrix1.Pin_11
  N18: U13.SEGDP, 8x8_LED_Matrix1.Pin_13
  N19: U13.SEGD, 8x8_LED_Matrix1.Pin_6

custom parts:
  8x8 LED Matrix 1388ASR: Red Color Common Anode 8x8 LED Matrix

// code stored in the sketch: a006resistencias.ino
/*
  Autor: Ramón Junquera
  
  Tema: Lectura y escritura de señales digitales
  
  Objetivo: Funcionamiento de las resistencias de seguridad y de la breadboard
  
  Material adicional: breadboard, led, resistencia, cables

  Descripción:
  El ejemplo es el mismo que el utilizado en el ejemplo de blink. Se hace parpadear un led conectado al pin 13.
  La diferencia es que utilizaremos una breadboard para montar un led externo y le pondremos una resistencia de seguridad.
  LED significa Light Emiting Diode. Son diodos que se iluminan cuando pasa la electricidad.
  Un led tiene polaridad. Si se conecta con la polaridad invertida puede quemarse.
  Sus conexiones se diferencian para poder conectar siempre correctamente.
  La pata más larga es el ánodo, o pata positiva. Siempre se conecta a la fuente de alimentación o pin.
  La pata más corta es el cátodo, o pata negativa. Siempre se conecta a tierra (GND).
  Un led siempre debe ir acompañado de una resistencia para proteger el microcontrolador de la placa.
  El rango intensidad adecuado para el correcto funcionamiento de un led es de 5 a 20mA.
  Para que un led se ilumine bien, sin llegar al límite, se considera que necesita 15mA (0.015A).
  Arduino trabaja con una diferencia de potencial (voltaje) de 5V.
  El led consume unos 2V, así que necesitamos una resistencia que consuma los otros 3.
  Puesto que V=I*R (Voltaje = Intensidad * Resistencia)
  Deducimos que R=V/I=3V/0.015A=200 ohmios.
  Si aumentamos la resistencia en un 10% (por seguridad) para asegurarnos que nunca llegaremos al límite máximo
  tenemos que necesitamos que un led siempre tenga asociada una resistencia de 220 ohmios.
  Distinguimos una resistencia de 220 ohmios porque tiene las siguientes bandas:
  - Banda 1 = roja = 2
  - Banda 2 = roja = 2
  - Banda 3 = negra = 0
  - Banda 4 = negra = multiplicador *1
  - Banda 5 = dorada = tolerancia +-5%
  Para que la resistencia haga su trabajo de reducción de voltaje debemos encadenar los elementos de la siguiente manera:
  - Pin o fuentee de alimentación (polo positivo)
  - Resistencia de 220 ohmios
  - Ánodo (pata larga) del led
  - Cátodo (pata corta) del led
  - Tierra (GND o polo negativo)
  Si queremos ser exactos, no todos los leds consumen el mismo voltaje. Depende del color. Esta es la tabla correcta:
    1.7V : rojo de bajo brillo
    1.9V : rojo de alto brillo, alta eficacia y baja corriente
    2.0V : naranja y amarillo
    2.1V : verde
    3.4V : blanco brilante, verde brillante y azul
    4.6V : azul brillante y leds especializados
  El led que está integrado en placa ya tiene tambien en placa su resistencia asociada.
  
  Resultado:
  El led externo parpadea al unísono con el que está integrado en placa.
*/

// the setup function runs once when you press reset or power the board
void setup() {
  //Configuramos el pin 13 como salida para poder escribir en él
  pinMode(13, OUTPUT);
}

// the loop function runs over and over again forever
void loop() {
  digitalWrite(13, HIGH);   //Encendemos el led
  delay(1000);              //Esperamos un segundo
  digitalWrite(13, LOW);    //Apagamos el led
  delay(1000);              //Esperamos otro segundo
}
