# Fritzing sketch UNOnano (saved by Fritzing 0.9.2b)
breadboards: 2

parts:
  Parte4 = Arduino Nano (Rev3.0)
  Parte5 = Arduino Uno (Rev3)
  LED4 = LED - 5mm [color="Infrared (850nm)" package="5 mm [THT]"]
  LED5 = LED - 5mm [color="Infrared (940nm)" package="5 mm [THT]"]
  LED6 = LED - 5mm [color="Red (633nm)" package="5 mm [THT]"]
  LED7 = LED - 5mm [color="Red (633nm)" package="5 mm [THT]"]
  R4 = Resistor [tolerance=±5% resistance=10k package="0805 [SMD]"]
  R5 = Resistor [tolerance=±5% resistance=220 package="0805 [SMD]"]
  R6 = Resistor [tolerance=±5% resistance=220 package="0805 [SMD]"]
  LED8 = LED - 5mm [color="Infrared (940nm)" package="5 mm [THT]"]
  R7 = Resistor [tolerance=±5% resistance=10k package="0805 [SMD]"]
  LED9 = LED - 5mm [color="Infrared (850nm)" package="5 mm [THT]"]
  C7 = Ceramic Capacitor [capacitance=10µF package="1206 [SMD, multilayer]"]
  C8 = Ceramic Capacitor [capacitance="100 nF" package="1206 [SMD, multilayer]"]
  U5 = 7-SEGMENT-4DIGIT [package=7-segment-4digit-5641]
  U6 = MAX7219 [package=dil24]
  R8 = Resistor [tolerance=±1% resistance=10k package=THT]

nets:
  GND: Parte4.GND, C7.1, C8.0, U6.GND, U6.GND2
  N1: Parte4.D2, LED8.anode, R7.Pin_1
  N2: Parte4.D3, LED5.anode, R4.Pin_1
  N3: Parte4.D4, LED7.anode
  N4: Parte4.D5, LED6.anode
  N5: Parte4.D7, U6.LOAD
  N6: Parte4.D8, U6.CLK
  N7: Parte4.D9, U6.DIN
  5V: Parte4.5V, C7.0, C8.1, U6.VCC, R8.Pin_1
  N8: Parte5.3V3, LED4.anode, LED9.anode
  N9: Parte5.GND, LED4.cathode, LED9.cathode
  N10: LED5.cathode, LED8.cathode
  N11: LED6.cathode, R5.Pin_0
  N12: LED7.cathode, R6.Pin_0
  N13: R4.Pin_0, R5.Pin_1, R6.Pin_1, R7.Pin_0
  N14: U5.DIG2, U6.DIG1
  N15: U5.DIG3, U6.DIG2
  N16: U5.DIG4, U6.DIG3
  N17: U5.A, U6.SEGA
  N18: U5.B, U6.SEGB
  N19: U5.C, U6.SEGC
  N20: U5.D, U6.SEGD
  N21: U5.E, U6.SEGE
  N22: U5.F, U6.SEGF
  N23: U5.G, U6.SEGG
  N24: U5.DP, U6.SEGDP
  N25: U5.DIG1, U6.DIG0
  N26: U6.ISET, R8.Pin_0

notes:
  Receptores
  Emisores

custom parts:
  7-SEGMENT-4DIGIT: if you need make parts, send me e-mail and write. Price 1 part=0.9 WMZ (http://www.wmtransfer.com/) ~ 0.9 Euro

// code stored in the sketch: a006resistencias.ino
/*
  Autor: Ramón Junquera
  
  Tema: Lectura y escritura de señales digitales
  
  Objetivo: Funcionamiento de las resistencias de seguridad y de la breadboard
  
  Material adicional: breadboard, led, resistencia, cables

  Descripción:
  El ejemplo es el mismo que el utilizado en el ejemplo de blink. Se hace parpadear un led conectado al pin 13.
  La diferencia es que utilizaremos una breadboard para montar un led externo y le pondremos una resistencia de seguridad.
  LED significa Light Emiting Diode. Son diodos que se iluminan cuando pasa la electricidad.
  Un led tiene polaridad. Si se conecta con la polaridad invertida puede quemarse.
  Sus conexiones se diferencian para poder conectar siempre correctamente.
  La pata más larga es el ánodo, o pata positiva. Siempre se conecta a la fuente de alimentación o pin.
  La pata más corta es el cátodo, o pata negativa. Siempre se conecta a tierra (GND).
  Un led siempre debe ir acompañado de una resistencia para proteger el microcontrolador de la placa.
  El rango intensidad adecuado para el correcto funcionamiento de un led es de 5 a 20mA.
  Para que un led se ilumine bien, sin llegar al límite, se considera que necesita 15mA (0.015A).
  Arduino trabaja con una diferencia de potencial (voltaje) de 5V.
  El led consume unos 2V, así que necesitamos una resistencia que consuma los otros 3.
  Puesto que V=I*R (Voltaje = Intensidad * Resistencia)
  Deducimos que R=V/I=3V/0.015A=200 ohmios.
  Si aumentamos la resistencia en un 10% (por seguridad) para asegurarnos que nunca llegaremos al límite máximo
  tenemos que necesitamos que un led siempre tenga asociada una resistencia de 220 ohmios.
  Distinguimos una resistencia de 220 ohmios porque tiene las siguientes bandas:
  - Banda 1 = roja = 2
  - Banda 2 = roja = 2
  - Banda 3 = negra = 0
  - Banda 4 = negra = multiplicador *1
  - Banda 5 = dorada = tolerancia +-5%
  Para que la resistencia haga su trabajo de reducción de voltaje debemos encadenar los elementos de la siguiente manera:
  - Pin o fuentee de alimentación (polo positivo)
  - Resistencia de 220 ohmios
  - Ánodo (pata larga) del led
  - Cátodo (pata corta) del led
  - Tierra (GND o polo negativo)
  Si queremos ser exactos, no todos los leds consumen el mismo voltaje. Depende del color. Esta es la tabla correcta:
    1.7V : rojo de bajo brillo
    1.9V : rojo de alto brillo, alta eficacia y baja corriente
    2.0V : naranja y amarillo
    2.1V : verde
    3.4V : blanco brilante, verde brillante y azul
    4.6V : azul brillante y leds especializados
  El led que está integrado en placa ya tiene tambien en placa su resistencia asociada.
  
  Resultado:
  El led externo parpadea al unísono con el que está integrado en placa.
*/

// the setup function runs once when you press reset or power the board
void setup() {
  //Configuramos el pin 13 como salida para poder escribir en él
  pinMode(13, OUTPUT);
}

// the loop function runs over and over again forever
void loop() {
  digitalWrite(13, HIGH);   //Encendemos el led
  delay(1000);              //Esperamos un segundo
  digitalWrite(13, LOW);    //Apagamos el led
  delay(1000);              //Esperamos otro segundo
}
