# Fritzing sketch io.display (saved by Fritzing 0.9.2b)
breadboards: 2

parts:
  Parte1 = Arduino Nano (Rev3.0)
  Parte2 = Arduino Uno (Rev3)
  R6 = Resistor [tolerance=±1% resistance=220 package=THT]
  LED8 = LED - 5mm [color="Red (633nm)" package="5 mm [THT]"]
  R9 = Resistor [tolerance=±1% resistance=220 package=THT]
  LED9 = LED - 5mm [color="Red (633nm)" package="5 mm [THT]"]
  LED10 = LED - 5mm [color="Infrared (940nm)" package="5 mm [THT]"]
  R10 = Resistor [tolerance=±1% resistance=220 package=THT]
  IR_Reciever_AX-1838HS2 = IR Reciever AX-1838HS
  keypad1 = Membrane Matrix Keypad
  LCD2 = LCD screen
  R14 = Resistor [tolerance=±1% resistance=1k package=THT]
  R12 = Resistor [tolerance=±1% resistance=220 package=THT]

nets:
  GND: Parte1.GND, LED8.cathode, IR_Reciever_AX-1838HS2.GND, LCD2.VSS, LCD2.R/W, LCD2.LED-, R14.Pin_0
  N1: Parte1.D2, R6.Pin_0
  N2: Parte1.D3, IR_Reciever_AX-1838HS2.OUT
  N3: Parte1.D7, LCD2.RS
  N4: Parte1.D8, LCD2.E
  N5: Parte1.D9, LCD2.DB4
  N6: Parte1.D10, LCD2.DB5
  N7: Parte1.D11/MOSI, LCD2.DB6
  N8: Parte1.D12/MISO, LCD2.DB7
  5V: Parte1.5V, IR_Reciever_AX-1838HS2.VCC, LCD2.LED+, R12.Pin_0
  N9: Parte2.D8, keypad1.Row_4
  N10: Parte2.D9_PWM, keypad1.Row_3
  N11: Parte2.D10_PWM/SS, keypad1.Row_2
  N12: Parte2.D11_PWM/MOSI, keypad1.Row_1
  N13: Parte2.GND, LED9.cathode, LED10.cathode
  N14: Parte2.D2, R9.Pin_0
  N15: Parte2.D3_PWM, R10.Pin_0
  N16: Parte2.D4, keypad1.Col_4
  N17: Parte2.D5_PWM, keypad1.Col_3
  N18: Parte2.D6_PWM, keypad1.Col_2
  N19: Parte2.D7, keypad1.Col_1
  N20: R6.Pin_1, LED8.anode
  N21: R9.Pin_1, LED9.anode
  N22: LED10.anode, R10.Pin_1
  N23: LCD2.VDD, R12.Pin_1
  N24: LCD2.V0, R14.Pin_1

custom parts:
  IR Reciever AX-1838HS: Basic infrared reciever
  Membrane Matrix Keypad: Membrane Matrix 4x4 Keypad

// code stored in the sketch: a006resistencias.ino
/*
  Autor: Ramón Junquera
  
  Tema: Lectura y escritura de señales digitales
  
  Objetivo: Funcionamiento de las resistencias de seguridad y de la breadboard
  
  Material adicional: breadboard, led, resistencia, cables

  Descripción:
  El ejemplo es el mismo que el utilizado en el ejemplo de blink. Se hace parpadear un led conectado al pin 13.
  La diferencia es que utilizaremos una breadboard para montar un led externo y le pondremos una resistencia de seguridad.
  LED significa Light Emiting Diode. Son diodos que se iluminan cuando pasa la electricidad.
  Un led tiene polaridad. Si se conecta con la polaridad invertida puede quemarse.
  Sus conexiones se diferencian para poder conectar siempre correctamente.
  La pata más larga es el ánodo, o pata positiva. Siempre se conecta a la fuente de alimentación o pin.
  La pata más corta es el cátodo, o pata negativa. Siempre se conecta a tierra (GND).
  Un led siempre debe ir acompañado de una resistencia para proteger el microcontrolador de la placa.
  El rango intensidad adecuado para el correcto funcionamiento de un led es de 5 a 20mA.
  Para que un led se ilumine bien, sin llegar al límite, se considera que necesita 15mA (0.015A).
  Arduino trabaja con una diferencia de potencial (voltaje) de 5V.
  El led consume unos 2V, así que necesitamos una resistencia que consuma los otros 3.
  Puesto que V=I*R (Voltaje = Intensidad * Resistencia)
  Deducimos que R=V/I=3V/0.015A=200 ohmios.
  Si aumentamos la resistencia en un 10% (por seguridad) para asegurarnos que nunca llegaremos al límite máximo
  tenemos que necesitamos que un led siempre tenga asociada una resistencia de 220 ohmios.
  Distinguimos una resistencia de 220 ohmios porque tiene las siguientes bandas:
  - Banda 1 = roja = 2
  - Banda 2 = roja = 2
  - Banda 3 = negra = 0
  - Banda 4 = negra = multiplicador *1
  - Banda 5 = dorada = tolerancia +-5%
  Para que la resistencia haga su trabajo de reducción de voltaje debemos encadenar los elementos de la siguiente manera:
  - Pin o fuentee de alimentación (polo positivo)
  - Resistencia de 220 ohmios
  - Ánodo (pata larga) del led
  - Cátodo (pata corta) del led
  - Tierra (GND o polo negativo)
  Si queremos ser exactos, no todos los leds consumen el mismo voltaje. Depende del color. Esta es la tabla correcta:
    1.7V : rojo de bajo brillo
    1.9V : rojo de alto brillo, alta eficacia y baja corriente
    2.0V : naranja y amarillo
    2.1V : verde
    3.4V : blanco brilante, verde brillante y azul
    4.6V : azul brillante y leds especializados
  El led que está integrado en placa ya tiene tambien en placa su resistencia asociada.
  
  Resultado:
  El led externo parpadea al unísono con el que está integrado en placa.
*/

// the setup function runs once when you press reset or power the board
void setup() {
  //Configuramos el pin 13 como salida para poder escribir en él
  pinMode(13, OUTPUT);
}

// the loop function runs over and over again forever
void loop() {
  digitalWrite(13, HIGH);   //Encendemos el led
  delay(1000);              //Esperamos un segundo
  digitalWrite(13, LOW);    //Apagamos el led
  delay(1000);              //Esperamos otro segundo
}
