# Fritzing sketch WemosLolin32Lite-Max98357A (saved by Fritzing 0.9.3b)
breadboards: 1

parts:
  S1 = Pushbutton [package="[THT]"]
  S2 = Pushbutton [package="[THT]"]
  Microphone1 = Microphone I2S INM441 MEMS
  MCU1 = Wemos Lolin32 Lite
  Part3 = Adafruit MAX98357A I2S 3W Class D Amplifier [part_number="Adafruit #3006"]
  SP2 = SPEAKER [package=pcb_mount_speaker]  # not connected

nets:
  N1: S1.Pin_1, S1.Pin_2, MCU1.pin_7
  GND: S1.Pin_3, S1.Pin_4, S2.Pin_3, S2.Pin_4, Microphone1.L/R, Microphone1.GND, MCU1.pin_13, Part3.GND, Part3.GAIN
  N2: S2.Pin_1, S2.Pin_2, MCU1.pin_26
  N3: Microphone1.WS, MCU1.pin_8, Part3.LRCLK
  N4: Microphone1.SCK, MCU1.pin_9, Part3.BCLK
  N5: Microphone1.SD, MCU1.pin_6
  VDD: Microphone1.VDD, MCU1.pin_28, Part3.VIN
  N6: MCU1.pin_25, Part3.DIN

custom parts:
  Microphone I2S INM441 MEMS: Microphone omni MH-ET, I2S INM441 MEMS
  Adafruit MAX98357A I2S 3W Class D Amplifier: Listen to this good news - we now have an all in one digital audio amp breakout board that works incredibly well with the Raspberry Pi! If you're looking for an easy and low cost way to get you digital sound files bumpin' then the MAX08357 I2S Amp Breakout is for you. It takes standard I2S digital audio input and, not only decodes it into analog, but also amplifies it directly into a speaker.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
