# Fritzing sketch StickCplus (saved by Fritzing 0.9.3b)

parts:
  J1 = Piezo Speaker  # not connected
  M5Stack+1 = M5Stick-C+
  M5Stack_microphone1 = Microphone SPM1423

nets:
  N1: M5Stack+1.G33, M5Stack_microphone1.CLK
  N2: M5Stack+1.G32, M5Stack_microphone1.DAT
  5V: M5Stack+1.5v, M5Stack_microphone1.5V
  GND: M5Stack+1.Gnd, M5Stack_microphone1.GND

custom parts:
  M5Stick-C+: M5Stick-C+ is a mini M5Stack, powered by ESP32 pico chip. It is a portable, easy-to-use, open source, IoT development board.
  Microphone SPM1423: M5Stack externel microphone SPM1423
