# Fritzing sketch WemosLolin32Lite (saved by Fritzing 0.9.3b)
breadboards: 1

parts:
  MCU3 = Wemos Lolin32 Lite
  S3 = Pushbutton [package="[THT]"]
  Part5 = Adafruit MAX98357A I2S 3W Class D Amplifier [part_number="Adafruit #3006"]
  SP1 = SPEAKER [package=pcb_mount_speaker]  # not connected

nets:
  N1: MCU3.pin_7, S3.Pin_3, S3.Pin_4
  N2: MCU3.pin_8, Part5.LRCLK
  N3: MCU3.pin_9, Part5.BCLK
  N4: MCU3.pin_13, S3.Pin_1, S3.Pin_2, Part5.GND, Part5.GAIN
  N5: MCU3.pin_25, Part5.DIN
  N6: MCU3.pin_28, Part5.VIN, Part5.SD_MODE

custom parts:
  Adafruit MAX98357A I2S 3W Class D Amplifier: Listen to this good news - we now have an all in one digital audio amp breakout board that works incredibly well with the Raspberry Pi! If you're looking for an easy and low cost way to get you digital sound files bumpin' then the MAX08357 I2S Amp Breakout is for you. It takes standard I2S digital audio input and, not only decodes it into analog, but also amplifies it directly into a speaker.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
