# Fritzing sketch WemosD1mini (saved by Fritzing 0.9.3b)
breadboards: 1

parts:
  WeMos_D1_Mini1 = WeMos D1 Mini  # not connected
  LED1 = LED - 5mm [color="Blue (430nm)" package="5 mm [THT]"]
  S1 = Pushbutton [package="[THT]"]
  LED2 = LED - 5mm [color="Green (555nm)" package="5 mm [THT]"]  # not connected

nets:
  N1: LED1.cathode, S1.Pin_1, S1.Pin_2
  N2: S1.Pin_3, S1.Pin_4
