# Fritzing sketch Nano (saved by Fritzing 0.9.3b)
breadboards: 1

parts:
  Parte4 = Arduino Nano (Rev3.0)
  Componente10 = Logic Level Converter Bi-Directional BOB-12009
  U9 = 2.4" TFT LCD screen, SPI, Touch-enabled
  Componente11 = Logic Level Converter Bi-Directional BOB-12009

nets:
  GND: Parte4.GND, Componente10.GND, U9.GND, Componente11.GND
  N1: Parte4.D2, Componente10.HV1
  N2: Parte4.D3, Componente10.HV2
  N3: Parte4.D4, Componente10.HV3
  N4: Parte4.D5, Componente10.HV4
  N5: Parte4.D6, Componente11.HV1
  N6: Parte4.D7, U9.SD_CS
  N7: Parte4.D11/MOSI, Componente11.HV2
  N8: Parte4.D12/MISO, Componente11.HV3
  5V: Parte4.5V, Componente10.HV, U9.LED, U9.VCC, Componente11.HV
  N9: Parte4.3V3, Componente10.LV, Componente11.LV
  N10: Parte4.D13/SCK, Componente11.HV4
  N11: Componente10.LV4, U9.DC
  N12: Componente10.LV3, U9.RESET
  N13: Componente10.LV2, U9.CS
  N14: Componente10.LV1, U9.T_IRQ
  N15: U9.T_DO, U9.SD_MISO, Componente11.LV3
  N16: U9.T_DIN, U9.SDA, U9.SD_MOSI, Componente11.LV2
  N17: U9.T_CS, Componente11.LV1
  N18: U9.T_CLK, U9.SCL, U9.SD_SCK, Componente11.LV4

custom parts:
  Logic Level Converter Bi-Directional BOB-12009: SparkFun product BOB-12009 If you’ve ever tried to connect a 3.3V device to a 5V system, you know what a challenge it can be. The SparkFun bi-directional logic level converter is a small device that safely steps down 5V signals to 3.3V AND steps up 3.3V to 5V at the same time. This level converter also works with 2.8V and 1.8V devices. What really separates this Logic level converter from our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
  2.4" TFT LCD screen, SPI, Touch-enabled: 2.4", ILI9341-based TFT LCD screen with touch-sensing using the XPT2046 controller, SPI-compatible. There is also an SD-card version that is non-touch enabled but uses exactly the same board and pinout. This part is for both, though it should be noted that the SD reader and the touch screen are mutually incompatible

// code stored in the sketch: a006resistencias.ino
/*
  Autor: Ramón Junquera
  
  Tema: Lectura y escritura de señales digitales
  
  Objetivo: Funcionamiento de las resistencias de seguridad y de la breadboard
  
  Material adicional: breadboard, led, resistencia, cables

  Descripción:
  El ejemplo es el mismo que el utilizado en el ejemplo de blink. Se hace parpadear un led conectado al pin 13.
  La diferencia es que utilizaremos una breadboard para montar un led externo y le pondremos una resistencia de seguridad.
  LED significa Light Emiting Diode. Son diodos que se iluminan cuando pasa la electricidad.
  Un led tiene polaridad. Si se conecta con la polaridad invertida puede quemarse.
  Sus conexiones se diferencian para poder conectar siempre correctamente.
  La pata más larga es el ánodo, o pata positiva. Siempre se conecta a la fuente de alimentación o pin.
  La pata más corta es el cátodo, o pata negativa. Siempre se conecta a tierra (GND).
  Un led siempre debe ir acompañado de una resistencia para proteger el microcontrolador de la placa.
  El rango intensidad adecuado para el correcto funcionamiento de un led es de 5 a 20mA.
  Para que un led se ilumine bien, sin llegar al límite, se considera que necesita 15mA (0.015A).
  Arduino trabaja con una diferencia de potencial (voltaje) de 5V.
  El led consume unos 2V, así que necesitamos una resistencia que consuma los otros 3.
  Puesto que V=I*R (Voltaje = Intensidad * Resistencia)
  Deducimos que R=V/I=3V/0.015A=200 ohmios.
  Si aumentamos la resistencia en un 10% (por seguridad) para asegurarnos que nunca llegaremos al límite máximo
  tenemos que necesitamos que un led siempre tenga asociada una resistencia de 220 ohmios.
  Distinguimos una resistencia de 220 ohmios porque tiene las siguientes bandas:
  - Banda 1 = roja = 2
  - Banda 2 = roja = 2
  - Banda 3 = negra = 0
  - Banda 4 = negra = multiplicador *1
  - Banda 5 = dorada = tolerancia +-5%
  Para que la resistencia haga su trabajo de reducción de voltaje debemos encadenar los elementos de la siguiente manera:
  - Pin o fuentee de alimentación (polo positivo)
  - Resistencia de 220 ohmios
  - Ánodo (pata larga) del led
  - Cátodo (pata corta) del led
  - Tierra (GND o polo negativo)
  Si queremos ser exactos, no todos los leds consumen el mismo voltaje. Depende del color. Esta es la tabla correcta:
    1.7V : rojo de bajo brillo
    1.9V : rojo de alto brillo, alta eficacia y baja corriente
    2.0V : naranja y amarillo
    2.1V : verde
    3.4V : blanco brilante, verde brillante y azul
    4.6V : azul brillante y leds especializados
  El led que está integrado en placa ya tiene tambien en placa su resistencia asociada.
  
  Resultado:
  El led externo parpadea al unísono con el que está integrado en placa.
*/

// the setup function runs once when you press reset or power the board
void setup() {
  //Configuramos el pin 13 como salida para poder escribir en él
  pinMode(13, OUTPUT);
}

// the loop function runs over and over again forever
void loop() {
  digitalWrite(13, HIGH);   //Encendemos el led
  delay(1000);              //Esperamos un segundo
  digitalWrite(13, LOW);    //Apagamos el led
  delay(1000);              //Esperamos otro segundo
}
