# Fritzing sketch Echo (saved by Fritzing 0.9.3b)

parts:
  M5Stack_Atom_Echo1 = M5Stack Atom Echo
  M5Stack_microphone1 = Microphone SPM1423

nets:
  N1: M5Stack_Atom_Echo1.G32, M5Stack_microphone1.CLK
  N2: M5Stack_Atom_Echo1.G26, M5Stack_microphone1.DAT
  5V: M5Stack_Atom_Echo1.5V, M5Stack_microphone1.5V
  N3: M5Stack_Atom_Echo1.G, M5Stack_microphone1.GND

custom parts:
  Microphone SPM1423: M5Stack externel microphone SPM1423
