# Fritzing sketch WemosLolinD32-PCM5102 (saved by Fritzing 0.9.3b)
breadboards: 1

parts:
  Microphone1 = Microphone I2S INM441 MEMS
  MCU1 = Wemos Lolin32 Lite
  Part2 = PCM5102  # not connected

nets:
  N1: Microphone1.L/R, Microphone1.GND, MCU1.pin_13
  N2: Microphone1.WS, MCU1.pin_17
  N3: Microphone1.SCK, MCU1.pin_11
  N4: Microphone1.SD, MCU1.pin_6
  N5: Microphone1.VDD, MCU1.pin_28

custom parts:
  Microphone I2S INM441 MEMS: Microphone omni MH-ET, I2S INM441 MEMS
  PCM5102: Audio DAC I2S with 3.5 jack
