# Fritzing sketch WemosLolin32Lite (saved by Fritzing 0.9.3b)
breadboards: 1

parts:
  S1 = Pushbutton [package="[THT]"]
  S2 = Pushbutton [package="[THT]"]
  J1 = Piezo Speaker
  Microphone1 = Microphone I2S INM441 MEMS
  MCU1 = Wemos Lolin32 Lite

nets:
  N1: S1.Pin_1, S1.Pin_2, MCU1.pin_7
  N2: S1.Pin_3, S1.Pin_4, S2.Pin_3, S2.Pin_4, J1.pin1, Microphone1.L/R, Microphone1.GND, MCU1.pin_13
  N3: S2.Pin_1, S2.Pin_2, MCU1.pin_9
  N4: J1.pin2, MCU1.pin_8
  N5: Microphone1.WS, MCU1.pin_17
  N6: Microphone1.SCK, MCU1.pin_11
  N7: Microphone1.SD, MCU1.pin_6
  N8: Microphone1.VDD, MCU1.pin_28

custom parts:
  Microphone I2S INM441 MEMS: Microphone omni MH-ET, I2S INM441 MEMS
