# Fritzing sketch WemosLolin32Lite (saved by Fritzing 0.9.3b)
breadboards: 1

parts:
  SP1 = SPEAKER [package=pcb_mount_speaker]  # not connected
  Part2 = Adafruit MAX98357A I2S 3W Class D Amplifier [part_number="Adafruit #3006"]
  MCU2 = Wemos Lolin32 Lite
  S2 = Pushbutton [package="[THT]"]

nets:
  N1: Part2.VIN, MCU2.pin_28
  N2: Part2.GND, Part2.GAIN, MCU2.pin_13, S2.Pin_1, S2.Pin_2
  N3: Part2.DIN, MCU2.pin_25
  N4: Part2.BCLK, MCU2.pin_9
  N5: Part2.LRCLK, MCU2.pin_8
  N6: MCU2.pin_7, S2.Pin_3, S2.Pin_4

custom parts:
  Adafruit MAX98357A I2S 3W Class D Amplifier: Listen to this good news - we now have an all in one digital audio amp breakout board that works incredibly well with the Raspberry Pi! If you're looking for an easy and low cost way to get you digital sound files bumpin' then the MAX08357 I2S Amp Breakout is for you. It takes standard I2S digital audio input and, not only decodes it into analog, but also amplifies it directly into a speaker.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
