# Fritzing sketch WeMosLolin32 (saved by Fritzing 0.9.3b)
breadboards: 1

parts:
  U3 = lolin
  clock1 = Tiny RTC I2C
  led_display3 = Catalex 4-digits led display

nets:
  VCC: U3.connector0, clock1.VCC, led_display3.VCC
  N1: U3.connector11, led_display3.CLK
  N2: U3.connector13, led_display3.DIO
  GND: U3.connector15, clock1.GND, led_display3.GND
  N3: U3.connector32, clock1.SDA
  N4: U3.connector33, clock1.SCL

custom parts:
  Tiny RTC I2C: Tiny RTC I2C Real Time
