# Fritzing sketch circuito de transferencia (saved by Fritzing 0.9.3b)
breadboards: 3

parts:
  Parte8 = RoJo FTDI programmer  # not connected
  Parte9 = RoJo ADP-01
  U12 = ESP8266 WiFi Module (ESP-'1) [part_number=ESP8266]
  Parte19 = RoJo FTDI programmer
  Parte20 = RoJo ESP8266 Adapter v1.0
  U15 = ESP8266 WiFi Module (ESP-'1) [part_number=ESP8266]
  Parte21 = RoJo FTDI programmer
  U16 = ESP8266 WiFi Module (ESP-'1) [part_number=ESP8266]

nets:
  N1: Parte9.E_RX, U12.RXD
  N2: Parte9.E_VCC, U12.VCC
  N3: Parte9.E_GPIO0, U12.GPIO0
  N4: Parte9.E_RST, U12.RST
  N5: Parte9.E_GPIO2, U12.GPIO2
  N6: Parte9.E_CH_PD, U12.CH_PD
  N7: Parte9.E_GND, U12.GND
  N8: Parte9.E_TX, U12.TXD
  GND: Parte19.GND, Parte20.GPIO0, Parte20.GND
  5V: Parte19.5V, Parte20.CHPD, Parte20.VCC
  N9: Parte19.TXD, Parte20.RXD
  N10: Parte19.RXD, Parte20.TXD
  N11: Parte20.E_RX, U15.RXD
  N12: Parte20.E_VCC, U15.VCC
  N13: Parte20.E_GPIO0, U15.GPIO0
  N14: Parte20.E_RST, U15.RST
  N15: Parte20.E_GPIO2, U15.GPIO2
  N16: Parte20.E_CH_PD, U15.CH_PD
  N17: Parte20.E_GND, U15.GND
  N18: Parte20.E_TX, U15.TXD
  GND_2: Parte21.GND, U16.GPIO0, U16.GND
  5V_2: Parte21.5V, U16.VCC, U16.CH_PD
  N19: Parte21.TXD, U16.RXD
  N20: Parte21.RXD, U16.TXD

notes:
  Con zócalo ADP-01
  FTDI a 5V
  Con zócalo Adapter v1.0
  FTDI a 3,3V
  Sin zócalo
  FTDI a 3.3V

custom parts:
  RoJo FTDI programmer: FTDI programmer. Selected 3.3V or 5V
  RoJo ADP-01: ESP8266 (ESP-01) breadboard adapter
  ESP8266 WiFi Module (ESP-'1): Generic WiFi Module based on the ESP8266 with onboard PCB antenna and UART communications
  RoJo ESP8266 Adapter v1.0: ESP8266 Adapter v1.0 Raj Bhatt for ESP-01

// code stored in the sketch: a006resistencias.ino
/*
  Autor: Ramón Junquera
  
  Tema: Lectura y escritura de señales digitales
  
  Objetivo: Funcionamiento de las resistencias de seguridad y de la breadboard
  
  Material adicional: breadboard, led, resistencia, cables

  Descripción:
  El ejemplo es el mismo que el utilizado en el ejemplo de blink. Se hace parpadear un led conectado al pin 13.
  La diferencia es que utilizaremos una breadboard para montar un led externo y le pondremos una resistencia de seguridad.
  LED significa Light Emiting Diode. Son diodos que se iluminan cuando pasa la electricidad.
  Un led tiene polaridad. Si se conecta con la polaridad invertida puede quemarse.
  Sus conexiones se diferencian para poder conectar siempre correctamente.
  La pata más larga es el ánodo, o pata positiva. Siempre se conecta a la fuente de alimentación o pin.
  La pata más corta es el cátodo, o pata negativa. Siempre se conecta a tierra (GND).
  Un led siempre debe ir acompañado de una resistencia para proteger el microcontrolador de la placa.
  El rango intensidad adecuado para el correcto funcionamiento de un led es de 5 a 20mA.
  Para que un led se ilumine bien, sin llegar al límite, se considera que necesita 15mA (0.015A).
  Arduino trabaja con una diferencia de potencial (voltaje) de 5V.
  El led consume unos 2V, así que necesitamos una resistencia que consuma los otros 3.
  Puesto que V=I*R (Voltaje = Intensidad * Resistencia)
  Deducimos que R=V/I=3V/0.015A=200 ohmios.
  Si aumentamos la resistencia en un 10% (por seguridad) para asegurarnos que nunca llegaremos al límite máximo
  tenemos que necesitamos que un led siempre tenga asociada una resistencia de 220 ohmios.
  Distinguimos una resistencia de 220 ohmios porque tiene las siguientes bandas:
  - Banda 1 = roja = 2
  - Banda 2 = roja = 2
  - Banda 3 = negra = 0
  - Banda 4 = negra = multiplicador *1
  - Banda 5 = dorada = tolerancia +-5%
  Para que la resistencia haga su trabajo de reducción de voltaje debemos encadenar los elementos de la siguiente manera:
  - Pin o fuentee de alimentación (polo positivo)
  - Resistencia de 220 ohmios
  - Ánodo (pata larga) del led
  - Cátodo (pata corta) del led
  - Tierra (GND o polo negativo)
  Si queremos ser exactos, no todos los leds consumen el mismo voltaje. Depende del color. Esta es la tabla correcta:
    1.7V : rojo de bajo brillo
    1.9V : rojo de alto brillo, alta eficacia y baja corriente
    2.0V : naranja y amarillo
    2.1V : verde
    3.4V : blanco brilante, verde brillante y azul
    4.6V : azul brillante y leds especializados
  El led que está integrado en placa ya tiene tambien en placa su resistencia asociada.
  
  Resultado:
  El led externo parpadea al unísono con el que está integrado en placa.
*/

// the setup function runs once when you press reset or power the board
void setup() {
  //Configuramos el pin 13 como salida para poder escribir en él
  pinMode(13, OUTPUT);
}

// the loop function runs over and over again forever
void loop() {
  digitalWrite(13, HIGH);   //Encendemos el led
  delay(1000);              //Esperamos un segundo
  digitalWrite(13, LOW);    //Apagamos el led
  delay(1000);              //Esperamos otro segundo
}
