# Fritzing sketch UNO (saved by Fritzing 0.9.3b)

parts:
  led_display1 = Catalex 4-digits led display
  Parte1 = Arduino Uno (Rev3)

nets:
  N1: led_display1.CLK, Parte1.D2
  N2: led_display1.DIO, Parte1.D3_PWM
  VCC: led_display1.VCC, Parte1.5V
  GND: led_display1.GND, Parte1.GND
