# Fritzing sketch UNO (saved by Fritzing 0.9.3b)
breadboards: 1

parts:
  Parte1 = Arduino Uno (Rev3)
  keypad1 = Membrane Matrix Keypad
  MOTOR1 = 28BYJ-48 Stepper Motor  # not connected
  X1 = X113647 Stepper Driver Board [package=board]
  U5 = 7-SEGMENT-4DIGIT [package=7-segment-4digit-5641]
  C8 = Ceramic Capacitor [capacitance=10µF package="1206 [SMD, multilayer]"]
  C9 = Ceramic Capacitor [capacitance="100 nF" package="1206 [SMD, multilayer]"]
  U6 = MAX7219 [package=dil24]
  R3 = Resistor [tolerance=±1% resistance=10k package=THT]
  VCC1 = Battery block 9V

nets:
  N1: Parte1.A0, U6.LOAD
  N2: Parte1.A1, U6.DIN
  N3: Parte1.A2, U6.CLK
  N4: Parte1.D8, keypad1.Col_2
  N5: Parte1.D9_PWM, keypad1.Col_1
  N6: Parte1.D10_PWM/SS, keypad1.Row_4
  N7: Parte1.D11_PWM/MOSI, keypad1.Row_3
  N8: Parte1.D12/MISO, keypad1.Row_2
  N9: Parte1.D13/SCK, keypad1.Row_1
  N10: Parte1.D2, X1.IN4
  N11: Parte1.D3_PWM, X1.IN3
  N12: Parte1.D4, X1.IN2
  N13: Parte1.D5_PWM, X1.IN1
  N14: Parte1.D6_PWM, keypad1.Col_4
  N15: Parte1.D7, keypad1.Col_3
  5V: Parte1.5V, C8.0, C9.1, U6.VCC, R3.Pin_1
  GND: Parte1.GND, X1.GND, C8.1, C9.0, U6.GND, U6.GND2, VCC1.-
  N16: Parte1.VIN, X1.+V, VCC1.+
  N17: U5.DIG2, U6.DIG1
  N18: U5.DIG3, U6.DIG2
  N19: U5.DIG4, U6.DIG3
  N20: U5.A, U6.SEGDP
  N21: U5.B, U6.SEGA
  N22: U5.C, U6.SEGB
  N23: U5.D, U6.SEGC
  N24: U5.E, U6.SEGD
  N25: U5.F, U6.SEGE
  N26: U5.G, U6.SEGF
  N27: U5.DP, U6.SEGG
  N28: U5.DIG1, U6.DIG0
  N29: U6.ISET, R3.Pin_0

custom parts:
  Membrane Matrix Keypad: Membrane Matrix 4x4 Keypad
  28BYJ-48 Stepper Motor: 28BYJ-48 gear-reduction stepper motor (small)
  X113647 Stepper Driver Board: A common stepper motor driver board based on ULN2003APG darlington array
  7-SEGMENT-4DIGIT: if you need make parts, send me e-mail and write. Price 1 part=0.9 WMZ (http://www.wmtransfer.com/) ~ 0.9 Euro

// code stored in the sketch: a006resistencias.ino
/*
  Autor: Ramón Junquera
  
  Tema: Lectura y escritura de señales digitales
  
  Objetivo: Funcionamiento de las resistencias de seguridad y de la breadboard
  
  Material adicional: breadboard, led, resistencia, cables

  Descripción:
  El ejemplo es el mismo que el utilizado en el ejemplo de blink. Se hace parpadear un led conectado al pin 13.
  La diferencia es que utilizaremos una breadboard para montar un led externo y le pondremos una resistencia de seguridad.
  LED significa Light Emiting Diode. Son diodos que se iluminan cuando pasa la electricidad.
  Un led tiene polaridad. Si se conecta con la polaridad invertida puede quemarse.
  Sus conexiones se diferencian para poder conectar siempre correctamente.
  La pata más larga es el ánodo, o pata positiva. Siempre se conecta a la fuente de alimentación o pin.
  La pata más corta es el cátodo, o pata negativa. Siempre se conecta a tierra (GND).
  Un led siempre debe ir acompañado de una resistencia para proteger el microcontrolador de la placa.
  El rango intensidad adecuado para el correcto funcionamiento de un led es de 5 a 20mA.
  Para que un led se ilumine bien, sin llegar al límite, se considera que necesita 15mA (0.015A).
  Arduino trabaja con una diferencia de potencial (voltaje) de 5V.
  El led consume unos 2V, así que necesitamos una resistencia que consuma los otros 3.
  Puesto que V=I*R (Voltaje = Intensidad * Resistencia)
  Deducimos que R=V/I=3V/0.015A=200 ohmios.
  Si aumentamos la resistencia en un 10% (por seguridad) para asegurarnos que nunca llegaremos al límite máximo
  tenemos que necesitamos que un led siempre tenga asociada una resistencia de 220 ohmios.
  Distinguimos una resistencia de 220 ohmios porque tiene las siguientes bandas:
  - Banda 1 = roja = 2
  - Banda 2 = roja = 2
  - Banda 3 = negra = 0
  - Banda 4 = negra = multiplicador *1
  - Banda 5 = dorada = tolerancia +-5%
  Para que la resistencia haga su trabajo de reducción de voltaje debemos encadenar los elementos de la siguiente manera:
  - Pin o fuentee de alimentación (polo positivo)
  - Resistencia de 220 ohmios
  - Ánodo (pata larga) del led
  - Cátodo (pata corta) del led
  - Tierra (GND o polo negativo)
  Si queremos ser exactos, no todos los leds consumen el mismo voltaje. Depende del color. Esta es la tabla correcta:
    1.7V : rojo de bajo brillo
    1.9V : rojo de alto brillo, alta eficacia y baja corriente
    2.0V : naranja y amarillo
    2.1V : verde
    3.4V : blanco brilante, verde brillante y azul
    4.6V : azul brillante y leds especializados
  El led que está integrado en placa ya tiene tambien en placa su resistencia asociada.
  
  Resultado:
  El led externo parpadea al unísono con el que está integrado en placa.
*/

// the setup function runs once when you press reset or power the board
void setup() {
  //Configuramos el pin 13 como salida para poder escribir en él
  pinMode(13, OUTPUT);
}

// the loop function runs over and over again forever
void loop() {
  digitalWrite(13, HIGH);   //Encendemos el led
  delay(1000);              //Esperamos un segundo
  digitalWrite(13, LOW);    //Apagamos el led
  delay(1000);              //Esperamos otro segundo
}
