# Fritzing sketch ESP21OLED (saved by Fritzing 0.9.3b)
breadboards: 1

parts:
  MCU2 = RoJo ESP32 OLED
  Componente2 = Adafruit VL530X Time of Flight Distance Sensor [part_number="Adafruit #3317"]
  Componente3 = Adafruit VL530X Time of Flight Distance Sensor [part_number="Adafruit #3317"]

nets:
  GND: MCU2.GND#0, Componente2.GND, Componente3.GND
  VCC: MCU2.5V#1, Componente2.VCC, Componente3.VCC
  N1: MCU2.21, Componente2.SDA, Componente3.SDA
  N2: MCU2.22, Componente2.SCL, Componente3.SCL
  N3: MCU2.19, Componente3.XSHUT
  N4: MCU2.23, Componente2.XSHUT

custom parts:
  Adafruit VL530X Time of Flight Distance Sensor: The VL53L0X is a Time of Flight distance sensor like no other you've used! The sensor contains a very tiny invisible laser source, and a matching sensor. The VL53L0X can detect the "time of flight", or how long the light has taken to bounce back to the sensor. Since it uses a very narrow light source, it is good for determining distance of only the surface directly in front of it. Unlike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
