# Fritzing sketch UNO (saved by Fritzing 0.9.3b)
breadboards: 1

parts:
  Componente7 = Logic Level Converter Bi-Directional BOB-12009
  Componente8 = Logic Level Converter Bi-Directional BOB-12009
  Componente9 = 3.5inch RPi Display
  microSD_Transflash6 = SparkFun - microSD Transflash
  Componente10 = Arduino Uno (Rev3)

nets:
  N1: Componente7.LV4, Componente9.SPI_CLK
  N2: Componente7.LV3, Componente9.SPI_MOSI
  GND: Componente7.GND, Componente8.GND, Componente9.GND, microSD_Transflash6.GND, Componente10.GND
  N3: Componente7.LV, Componente8.LV, Componente10.3V3
  N4: Componente7.LV2, Componente9.SPI_MISO
  N5: Componente7.LV1, Componente9.TP_IRQ
  N6: Componente7.HV1, Componente10.D2
  N7: Componente7.HV2, microSD_Transflash6.DO, Componente10.D12/MISO
  5V: Componente7.HV, Componente8.HV, Componente9.5V, microSD_Transflash6.VCC, Componente10.5V
  N8: Componente7.HV3, microSD_Transflash6.DI, Componente10.D11_PWM/MOSI
  N9: Componente7.HV4, microSD_Transflash6.SCK, Componente10.D13/SCK
  N10: Componente8.LV4, Componente9.TP_SPI_CS
  N11: Componente8.LV3, Componente9.LCD_DC
  N12: Componente8.LV2, Componente9.RST
  N13: Componente8.LV1, Componente9.LCD_SPI_CS
  N14: Componente8.HV1, Componente10.D3_PWM
  N15: Componente8.HV2, Componente10.D4
  N16: Componente8.HV3, Componente10.D5_PWM
  N17: Componente8.HV4, Componente10.D6_PWM
  N18: microSD_Transflash6.CS, Componente10.D7

custom parts:
  Logic Level Converter Bi-Directional BOB-12009: SparkFun product BOB-12009 If you’ve ever tried to connect a 3.3V device to a 5V system, you know what a challenge it can be. The SparkFun bi-directional logic level converter is a small device that safely steps down 5V signals to 3.3V AND steps up 3.3V to 5V at the same time. This level converter also works with 2.8V and 1.8V devices. What really separates this Logic level converter from our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
  3.5inch RPi Display: Display TFT 3.5" 480x320 with touchpanel for RPi

// code stored in the sketch: a006resistencias.ino
/*
  Autor: Ramón Junquera
  
  Tema: Lectura y escritura de señales digitales
  
  Objetivo: Funcionamiento de las resistencias de seguridad y de la breadboard
  
  Material adicional: breadboard, led, resistencia, cables

  Descripción:
  El ejemplo es el mismo que el utilizado en el ejemplo de blink. Se hace parpadear un led conectado al pin 13.
  La diferencia es que utilizaremos una breadboard para montar un led externo y le pondremos una resistencia de seguridad.
  LED significa Light Emiting Diode. Son diodos que se iluminan cuando pasa la electricidad.
  Un led tiene polaridad. Si se conecta con la polaridad invertida puede quemarse.
  Sus conexiones se diferencian para poder conectar siempre correctamente.
  La pata más larga es el ánodo, o pata positiva. Siempre se conecta a la fuente de alimentación o pin.
  La pata más corta es el cátodo, o pata negativa. Siempre se conecta a tierra (GND).
  Un led siempre debe ir acompañado de una resistencia para proteger el microcontrolador de la placa.
  El rango intensidad adecuado para el correcto funcionamiento de un led es de 5 a 20mA.
  Para que un led se ilumine bien, sin llegar al límite, se considera que necesita 15mA (0.015A).
  Arduino trabaja con una diferencia de potencial (voltaje) de 5V.
  El led consume unos 2V, así que necesitamos una resistencia que consuma los otros 3.
  Puesto que V=I*R (Voltaje = Intensidad * Resistencia)
  Deducimos que R=V/I=3V/0.015A=200 ohmios.
  Si aumentamos la resistencia en un 10% (por seguridad) para asegurarnos que nunca llegaremos al límite máximo
  tenemos que necesitamos que un led siempre tenga asociada una resistencia de 220 ohmios.
  Distinguimos una resistencia de 220 ohmios porque tiene las siguientes bandas:
  - Banda 1 = roja = 2
  - Banda 2 = roja = 2
  - Banda 3 = negra = 0
  - Banda 4 = negra = multiplicador *1
  - Banda 5 = dorada = tolerancia +-5%
  Para que la resistencia haga su trabajo de reducción de voltaje debemos encadenar los elementos de la siguiente manera:
  - Pin o fuentee de alimentación (polo positivo)
  - Resistencia de 220 ohmios
  - Ánodo (pata larga) del led
  - Cátodo (pata corta) del led
  - Tierra (GND o polo negativo)
  Si queremos ser exactos, no todos los leds consumen el mismo voltaje. Depende del color. Esta es la tabla correcta:
    1.7V : rojo de bajo brillo
    1.9V : rojo de alto brillo, alta eficacia y baja corriente
    2.0V : naranja y amarillo
    2.1V : verde
    3.4V : blanco brilante, verde brillante y azul
    4.6V : azul brillante y leds especializados
  El led que está integrado en placa ya tiene tambien en placa su resistencia asociada.
  
  Resultado:
  El led externo parpadea al unísono con el que está integrado en placa.
*/

// the setup function runs once when you press reset or power the board
void setup() {
  //Configuramos el pin 13 como salida para poder escribir en él
  pinMode(13, OUTPUT);
}

// the loop function runs over and over again forever
void loop() {
  digitalWrite(13, HIGH);   //Encendemos el led
  delay(1000);              //Esperamos un segundo
  digitalWrite(13, LOW);    //Apagamos el led
  delay(1000);              //Esperamos otro segundo
}
