# Fritzing sketch Mega (saved by Fritzing 0.9.3b)
breadboards: 1

parts:
  Componente1 = Arduino Mega ADK (Rev3)
  microSD_Transflash3 = SparkFun - microSD Transflash
  OLED_I2C2 = OLED 128x32 I2C Monochrome Display
  keypad1 = Membrane Matrix Keypad

nets:
  N1: Componente1.D21/SCL, OLED_I2C2.SCK
  N2: Componente1.D20/SDA, OLED_I2C2.SDA
  N3: Componente1.D13_PWM, keypad1.Row_1
  N4: Componente1.D12_PWM, keypad1.Row_2
  N5: Componente1.D11_PWM, keypad1.Row_3
  N6: Componente1.D10_PWM, keypad1.Row_4
  N7: Componente1.D9_PWM, keypad1.Col_1
  N8: Componente1.D8_PWM, keypad1.Col_2
  N9: Componente1.D2_PWM, microSD_Transflash3.CS
  N10: Componente1.D3_PWM, OLED_I2C2.VDD
  N11: Componente1.D6_PWM, keypad1.Col_4
  N12: Componente1.D7_PWM, keypad1.Col_3
  5V: Componente1.5V, microSD_Transflash3.VCC
  N13: Componente1.D50/MISO, microSD_Transflash3.DO
  N14: Componente1.D51/MOSI, microSD_Transflash3.DI
  N15: Componente1.D52/SCK, microSD_Transflash3.SCK
  GND: Componente1.GND, microSD_Transflash3.GND, OLED_I2C2.GND

custom parts:
  Membrane Matrix Keypad: Membrane Matrix 4x4 Keypad

// code stored in the sketch: a006resistencias.ino
/*
  Autor: Ramón Junquera
  
  Tema: Lectura y escritura de señales digitales
  
  Objetivo: Funcionamiento de las resistencias de seguridad y de la breadboard
  
  Material adicional: breadboard, led, resistencia, cables

  Descripción:
  El ejemplo es el mismo que el utilizado en el ejemplo de blink. Se hace parpadear un led conectado al pin 13.
  La diferencia es que utilizaremos una breadboard para montar un led externo y le pondremos una resistencia de seguridad.
  LED significa Light Emiting Diode. Son diodos que se iluminan cuando pasa la electricidad.
  Un led tiene polaridad. Si se conecta con la polaridad invertida puede quemarse.
  Sus conexiones se diferencian para poder conectar siempre correctamente.
  La pata más larga es el ánodo, o pata positiva. Siempre se conecta a la fuente de alimentación o pin.
  La pata más corta es el cátodo, o pata negativa. Siempre se conecta a tierra (GND).
  Un led siempre debe ir acompañado de una resistencia para proteger el microcontrolador de la placa.
  El rango intensidad adecuado para el correcto funcionamiento de un led es de 5 a 20mA.
  Para que un led se ilumine bien, sin llegar al límite, se considera que necesita 15mA (0.015A).
  Arduino trabaja con una diferencia de potencial (voltaje) de 5V.
  El led consume unos 2V, así que necesitamos una resistencia que consuma los otros 3.
  Puesto que V=I*R (Voltaje = Intensidad * Resistencia)
  Deducimos que R=V/I=3V/0.015A=200 ohmios.
  Si aumentamos la resistencia en un 10% (por seguridad) para asegurarnos que nunca llegaremos al límite máximo
  tenemos que necesitamos que un led siempre tenga asociada una resistencia de 220 ohmios.
  Distinguimos una resistencia de 220 ohmios porque tiene las siguientes bandas:
  - Banda 1 = roja = 2
  - Banda 2 = roja = 2
  - Banda 3 = negra = 0
  - Banda 4 = negra = multiplicador *1
  - Banda 5 = dorada = tolerancia +-5%
  Para que la resistencia haga su trabajo de reducción de voltaje debemos encadenar los elementos de la siguiente manera:
  - Pin o fuentee de alimentación (polo positivo)
  - Resistencia de 220 ohmios
  - Ánodo (pata larga) del led
  - Cátodo (pata corta) del led
  - Tierra (GND o polo negativo)
  Si queremos ser exactos, no todos los leds consumen el mismo voltaje. Depende del color. Esta es la tabla correcta:
    1.7V : rojo de bajo brillo
    1.9V : rojo de alto brillo, alta eficacia y baja corriente
    2.0V : naranja y amarillo
    2.1V : verde
    3.4V : blanco brilante, verde brillante y azul
    4.6V : azul brillante y leds especializados
  El led que está integrado en placa ya tiene tambien en placa su resistencia asociada.
  
  Resultado:
  El led externo parpadea al unísono con el que está integrado en placa.
*/

// the setup function runs once when you press reset or power the board
void setup() {
  //Configuramos el pin 13 como salida para poder escribir en él
  pinMode(13, OUTPUT);
}

// the loop function runs over and over again forever
void loop() {
  digitalWrite(13, HIGH);   //Encendemos el led
  delay(1000);              //Esperamos un segundo
  digitalWrite(13, LOW);    //Apagamos el led
  delay(1000);              //Esperamos otro segundo
}
