# Fritzing sketch ESP21OLED (saved by Fritzing 0.9.3b)
breadboards: 1

parts:
  Componente1 = Adafruit VL530X Time of Flight Distance Sensor [part_number="Adafruit #3317"]
  MCU1 = RoJo ESP32 OLED

nets:
  N1: Componente1.VCC, MCU1.5V#1
  N2: Componente1.GND, MCU1.GND#0
  N3: Componente1.SCL, MCU1.22
  N4: Componente1.SDA, MCU1.21
  N5: Componente1.XSHUT, MCU1.19

custom parts:
  Adafruit VL530X Time of Flight Distance Sensor: The VL53L0X is a Time of Flight distance sensor like no other you've used! The sensor contains a very tiny invisible laser source, and a matching sensor. The VL53L0X can detect the "time of flight", or how long the light has taken to bounce back to the sensor. Since it uses a very narrow light source, it is good for determining distance of only the surface directly in front of it. Unlike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
