# Fritzing sketch WemosLolin32Lite-PCM5102 (saved by Fritzing 0.9.3b)
breadboards: 1

parts:
  S1 = Pushbutton [package="[THT]"]
  S2 = Pushbutton [package="[THT]"]
  Microphone1 = Microphone I2S INM441 MEMS
  MCU1 = Wemos Lolin32 Lite
  Part2 = PCM5102  # not connected

nets:
  N1: S1.Pin_1, S1.Pin_2, MCU1.pin_7
  N2: S1.Pin_3, S1.Pin_4, S2.Pin_3, S2.Pin_4, Microphone1.L/R, Microphone1.GND, MCU1.pin_13
  N3: S2.Pin_1, S2.Pin_2, MCU1.pin_26
  N4: Microphone1.WS, MCU1.pin_8
  N5: Microphone1.SCK, MCU1.pin_9
  N6: Microphone1.SD, MCU1.pin_6
  N7: Microphone1.VDD, MCU1.pin_28

custom parts:
  Microphone I2S INM441 MEMS: Microphone omni MH-ET, I2S INM441 MEMS
  PCM5102: Audio DAC I2S with 3.5 jack
