# Fritzing sketch WemosLolin32Lite-PCM5102 (saved by Fritzing 0.9.3b)
breadboards: 1

parts:
  MCU2 = Wemos Lolin32 Lite
  S2 = Pushbutton [package="[THT]"]
  Part3 = PCM5102  # not connected

nets:
  N1: MCU2.pin_7, S2.Pin_3, S2.Pin_4
  N2: MCU2.pin_13, S2.Pin_1, S2.Pin_2

custom parts:
  PCM5102: Audio DAC I2S with 3.5 jack
